// Logisim project Lab3.circ as structural Verilog: 7 circuits, main circuit ASL
module ASL (
  input  A2,
  input  A1,
  input  A0,
  input  A3,
  output B3,
  output B2,
  output B1,
  output B0
);

  wire and_1_out, and_3_out, and_4_out, and_6_out, not_1_out;

  not not_1 (not_1_out, 1'b0);
  and and_1 (and_1_out, A3, 1'b0);
  and and_2 (B3, not_1_out, A2);
  and and_3 (and_3_out, A2, 1'b0);
  or or_1 (B2, and_1_out, and_4_out);
  and and_4 (and_4_out, not_1_out, A1);
  and and_5 (B0, A1, 1'b0);
  or or_2 (B1, and_3_out, and_6_out);
  and and_6 (and_6_out, not_1_out, A0);

  // Notes on the sheet:
  //   0 for left
endmodule

module ASR (
  input  A3,
  input  A2,
  input  A1,
  input  A0,
  output B3,
  output B2,
  output B1,
  output B0
);

  wire and_1_out, and_3_out, and_4_out, and_6_out, not_1_out;

  not not_1 (not_1_out, 1'b1);
  and and_1 (and_1_out, A3, 1'b1);
  and and_2 (B3, not_1_out, A2);
  and and_3 (and_3_out, A2, 1'b1);
  or or_1 (B2, and_1_out, and_4_out);
  and and_4 (and_4_out, not_1_out, A1);
  and and_5 (B0, A1, 1'b1);
  or or_2 (B1, and_3_out, and_6_out);
  and and_6 (and_6_out, not_1_out, A0);

  // Notes on the sheet:
  //   1 for right
endmodule

module XOR4 (
  input  A0,
  input  B0,
  input  A1,
  input  B1,
  input  A2,
  input  B2,
  input  A3,
  input  B3,
  output C0,
  output C1,
  output C2,
  output C3
);

  xor xor_1 (C0, A0, B0);
  xor xor_2 (C1, A1, B1);
  xor xor_3 (C2, A2, B2);
  xor xor_4 (C3, A3, B3);
endmodule

module HA (
  input  A,
  input  B,
  output S,
  output C
);

  xor xor_1 (S, A, B);
  and and_1 (C, A, B);
endmodule

module TWOS_COMP (
  input  A3,
  input  A2,
  input  A1,
  input  A0,
  output B3,
  output B2,
  output B1,
  output B0
);

  wire and_1_out, and_2_out, and_3_out, and_4_out, and_5_out, and_6_out, and_7_out, not_1_out, not_2_out,
       not_3_out, not_4_out;

  not not_1 (not_1_out, A3);
  not not_2 (not_2_out, A2);
  not not_3 (not_3_out, A1);
  not not_4 (not_4_out, A0);
  and and_1 (and_1_out, not_1_out, A2);
  and and_2 (and_2_out, not_1_out, A1);
  and and_3 (and_3_out, not_1_out, A0);
  and and_4 (and_4_out, A3, not_2_out, not_3_out, not_4_out);
  and and_5 (and_5_out, A2, not_3_out, not_4_out);
  and and_6 (and_6_out, not_2_out, A0);
  and and_7 (and_7_out, not_2_out, A1);
  or or_1 (B3, and_1_out, and_2_out, and_3_out, and_4_out);
  or or_2 (B2, and_5_out, and_6_out, and_7_out);
  xor xor_1 (B1, A1, A0);

  assign B0 = A0;

  // Notes on the sheet:
  //   From Kmap: D
  //   From Kmap: !AB + !AC + !AD + A!B!C!D
  //   From Kmap: B!C!D + !BD + !BC
  //   From Kmap: !CD + C!D
  //   Unsimplified SOP B0: a3'a2'a1'a0 + a3'a2'a1a0' + a3'a2'a1a0 + a3'a2a1'a0'
  //   Unsimplified SOP B1: a3'a2'a1'a0 + a3'a2'a1a0' + a3'a2'a1a0 + a3'a2a1'a0' + a3a2'a1'a0 + a3a2'a1a0' + a3a2'a1a0 + a3a2a1'a0'
  //   Unsimplified SOP B2: a3'a2'a1'a0 + a3'a2'a1a0' + a3'a2a1'a0 + a3'a2a1a0' + a3a2'a1'a0 + a3a2'a1a0' + a3a2a1'a0 + a3a2a1a0'
  //   Unsimplified SOP B3: a3'a2'a1'a0 + a3'a2'a1a0 + a3'a2a1'a0 + a3'a2a1a0 + a3a2'a1'a0 + a3a2'a1a0 + a3a2a1'a0 + a3a3a1a0
  //   + a3'a2a1'a0 +a3'a2a1a0'+ a3'a2a1a0 + a3a2'a1'a0'
endmodule

module FA (
  input  A,
  input  B,
  input  C_in,
  output Sum,
  output Carry
);

  wire ha_1_c, ha_1_s, ha_2_c;

  HA ha_1 (.A(B), .B(A), .S(ha_1_s), .C(ha_1_c));
  HA ha_2 (.A(C_in), .B(ha_1_s), .S(Sum), .C(ha_2_c));
  or or_1 (Carry, ha_2_c, ha_1_c);
endmodule

module ADD_SUB (
  input  SUB_ADD,
  input  ENABLE,
  input  B0,
  input  A0,
  input  B1,
  input  A1,
  input  B2,
  input  A2,
  input  B3,
  input  A3,
  output S0,
  output S1,
  output S2,
  output S3,
  output Carry,
  output GT,
  output EQ,
  output LT,
  output C_out
);

  wire fa_1_carry, fa_1_sum, fa_2_carry, fa_2_sum, fa_3_carry, fa_3_sum, fa_4_carry, fa_4_sum, not_1_out,
       not_2_out, or_1_out, xor_1_out, xor_2_out, xor_3_out, xor_4_out;

  xor xor_1 (xor_1_out, B0, SUB_ADD);
  xor xor_2 (xor_2_out, B1, SUB_ADD);
  xor xor_3 (xor_3_out, B2, SUB_ADD);
  xor xor_4 (xor_4_out, B3, SUB_ADD);
  FA fa_1 (.A(xor_1_out), .B(A0), .C_in(SUB_ADD), .Sum(fa_1_sum), .Carry(fa_1_carry));
  FA fa_2 (.A(xor_2_out), .B(A1), .C_in(fa_1_carry), .Sum(fa_2_sum), .Carry(fa_2_carry));
  and and_1 (GT, not_2_out, not_1_out);
  not not_1 (not_1_out, EQ);
  not not_2 (not_2_out, LT);
  FA fa_3 (.A(xor_3_out), .B(A2), .C_in(fa_2_carry), .Sum(fa_3_sum), .Carry(fa_3_carry));
  assign S0 = ENABLE ? fa_1_sum : 1'bz;  // Controlled_Buffer controlled_buffer_1
  assign S1 = ENABLE ? fa_2_sum : 1'bz;  // Controlled_Buffer controlled_buffer_2
  assign S2 = ENABLE ? fa_3_sum : 1'bz;  // Controlled_Buffer controlled_buffer_3
  assign Carry = ENABLE ? fa_4_carry : 1'bz;  // Controlled_Buffer controlled_buffer_4
  assign LT = ENABLE ? fa_4_sum : 1'bz;  // Controlled_Buffer controlled_buffer_5
  FA fa_4 (.A(xor_4_out), .B(A3), .C_in(fa_3_carry), .Sum(fa_4_sum), .Carry(fa_4_carry));
  or or_1 (or_1_out, S0, S1, S2, LT);
  not not_3 (EQ, or_1_out);

  assign S3 = LT;
endmodule
