// Logisim project Lab6.circ as structural Verilog: 5 circuits, main circuit SR_GATES
module SR_GATES (
  input  RESET,
  input  SET,
  output Q,
  output NOT_Q
);

  nor nor_1 (Q, RESET, NOT_Q);
  nor nor_2 (NOT_Q, Q, SET);
endmodule

module SR_LATCH (
  input  RESET,
  input  SET,
  output NOT_Q,
  output Q
);

  _7402 #(.ShowInternalStructure("true")) u_7402_1 (
    .pin1(NOT_Q), .pin2(Q), .pin3(SET), .pin4(Q), .pin5(NOT_Q), .pin6(RESET));  // open: pin13, pin12, pin11, pin10, pin9, pin8
endmodule

module DFF_GATES (
  input  in_1,
  input  in_2,
  output out_3,
  output out_4
);

  wire and_1_out, and_2_out, not_1_out;

  not not_1 (not_1_out, in_1);
  and and_1 (and_1_out, not_1_out, in_2);
  and and_2 (and_2_out, in_2, in_1);
  SR_LATCH sr_latch_1 (.RESET(and_1_out), .SET(and_2_out), .NOT_Q(out_3), .Q(out_4));
endmodule

module DFF (
  input  D,
  input  CLK,
  output Q,
  output NOT_Q
);

  wire n7400_1_pin3, n7400_1_pin11, not_1_out;

  not not_1 (not_1_out, D);
  _7400 #(.ShowInternalStructure("true")) u_7400_1 (
    .pin1(not_1_out), .pin2(CLK), .pin3(n7400_1_pin3), .pin4(n7400_1_pin3), .pin5(NOT_Q), .pin6(Q),
    .pin13(CLK), .pin12(D), .pin11(n7400_1_pin11), .pin10(n7400_1_pin11), .pin9(Q), .pin8(NOT_Q));
endmodule

module REG4 (
  input  CLK,
  input  ENABLE,
  input  D0,
  input  D1,
  input  D2,
  input  D3,
  output Q0,
  output NOT_Q0,
  output Q1,
  output NOT_Q1,
  output Q2,
  output NOT_Q2,
  output Q3,
  output NOT_Q3
);

  wire and_1_out, and_2_out, and_3_out, and_4_out, not_1_out, not_2_out, not_3_out, not_4_out;

  not not_1 (not_1_out, D0);
  and and_1 (and_1_out, not_1_out, ENABLE);
  not not_2 (not_2_out, D1);
  and and_2 (and_2_out, not_2_out, ENABLE);
  not not_3 (not_3_out, D2);
  and and_3 (and_3_out, not_3_out, ENABLE);
  not not_4 (not_4_out, D3);
  and and_4 (and_4_out, not_4_out, ENABLE);
  DFF dff_1 (.D(and_1_out), .CLK(CLK), .Q(Q0), .NOT_Q(NOT_Q0));
  DFF dff_2 (.D(and_2_out), .CLK(CLK), .Q(Q1), .NOT_Q(NOT_Q1));
  DFF dff_3 (.D(and_3_out), .CLK(CLK), .Q(Q2), .NOT_Q(NOT_Q2));
  DFF dff_4 (.D(and_4_out), .CLK(CLK), .Q(Q3), .NOT_Q(NOT_Q3));
endmodule
