// Logisim project Lab8.circ as structural Verilog: 2 circuits, main circuit main
module main (
  input  A3,
  input  A2,
  input  A1,
  input  A0,
  input  I3,
  input  I2,
  input  I1,
  input  I0,
  input  B3,
  input  B2,
  input  B1,
  input  B0,
  output C0,
  output C1,
  output C2,
  output C3,
  output Carry,
  output Greater_Than,
  output Equal,
  output Less_Than
);

  wire add_sub_1_carry, add_sub_1_eq, add_sub_1_gt, add_sub_1_lt, add_sub_1_s0, add_sub_1_s1, add_sub_1_s2,
       add_sub_1_s3, asl_1_b0, asl_1_b1, asl_1_b2, asl_1_b3, asr_1_b0, asr_1_b1, asr_1_b2, asr_1_b3,
       decoder_1_out1, decoder_1_out2, decoder_1_out3, decoder_1_out4, decoder_1_out5, decoder_1_out6,
       decoder_1_out7, or_1_out, twos_comp_1_b0, twos_comp_1_b1, twos_comp_1_b2, twos_comp_1_b3, xor4_1_c0,
       xor4_1_c1, xor4_1_c2, xor4_1_c3;

  ASR asr_1 (.A3(A3), .A2(A2), .A1(A1), .A0(A0), .B3(asr_1_b3), .B2(asr_1_b2), .B1(asr_1_b1), .B0(asr_1_b0));
  ASL asl_1 (.A2(A2), .A1(A1), .A0(A0), .A3(A3), .B3(asl_1_b3), .B2(asl_1_b2), .B1(asl_1_b1), .B0(asl_1_b0));
  TWOS_COMP twos_comp_1 (
    .A3(A3), .A2(A2), .A1(A1), .A0(A0), .B3(twos_comp_1_b3), .B2(twos_comp_1_b2), .B1(twos_comp_1_b1),
    .B0(twos_comp_1_b0));
  Decoder #(.enable("false"), .select(4)) decoder_1 (
    .out1(decoder_1_out1), .out2(decoder_1_out2), .out3(decoder_1_out3), .out4(decoder_1_out4),
    .out5(decoder_1_out5), .out6(decoder_1_out6), .out7(decoder_1_out7), .sel({I3, I2, I1, I0}));  // open: out0, out8, out9, out10, out11, out12, out13, out14, out15
  XOR4 xor4_1 (
    .A0(A0), .B0(B0), .A1(A1), .B1(B1), .A2(A2), .B2(B2), .A3(A3), .B3(B3), .C0(xor4_1_c0), .C1(xor4_1_c1),
    .C2(xor4_1_c2), .C3(xor4_1_c3));
  ADD_SUB add_sub_1 (
    .SUB_ADD(decoder_1_out2), .ENABLE(1'b1), .B0(B0), .A0(A0), .B1(B1), .A1(A1), .B2(B2), .A2(A2), .B3(B3),
    .A3(A3), .S0(add_sub_1_s0), .S1(add_sub_1_s1), .S2(add_sub_1_s2), .S3(add_sub_1_s3),
    .Carry(add_sub_1_carry), .GT(add_sub_1_gt), .EQ(add_sub_1_eq), .LT(add_sub_1_lt));  // open: C_out
  assign C3 = decoder_1_out7 ? asr_1_b3 : 1'bz;  // Controlled_Buffer controlled_buffer_1
  assign C2 = decoder_1_out7 ? asr_1_b2 : 1'bz;  // Controlled_Buffer controlled_buffer_2
  assign C1 = decoder_1_out7 ? asr_1_b1 : 1'bz;  // Controlled_Buffer controlled_buffer_3
  assign C0 = decoder_1_out7 ? asr_1_b0 : 1'bz;  // Controlled_Buffer controlled_buffer_4
  assign C3 = decoder_1_out6 ? asl_1_b3 : 1'bz;  // Controlled_Buffer controlled_buffer_5
  assign C2 = decoder_1_out6 ? asl_1_b2 : 1'bz;  // Controlled_Buffer controlled_buffer_6
  assign C1 = decoder_1_out6 ? asl_1_b1 : 1'bz;  // Controlled_Buffer controlled_buffer_7
  assign C0 = decoder_1_out6 ? asl_1_b0 : 1'bz;  // Controlled_Buffer controlled_buffer_8
  assign C3 = decoder_1_out5 ? twos_comp_1_b3 : 1'bz;  // Controlled_Buffer controlled_buffer_9
  assign C2 = decoder_1_out5 ? twos_comp_1_b2 : 1'bz;  // Controlled_Buffer controlled_buffer_10
  assign C1 = decoder_1_out5 ? twos_comp_1_b1 : 1'bz;  // Controlled_Buffer controlled_buffer_11
  assign C0 = decoder_1_out5 ? twos_comp_1_b0 : 1'bz;  // Controlled_Buffer controlled_buffer_12
  assign C0 = decoder_1_out4 ? xor4_1_c0 : 1'bz;  // Controlled_Buffer controlled_buffer_13
  assign C1 = decoder_1_out4 ? xor4_1_c1 : 1'bz;  // Controlled_Buffer controlled_buffer_14
  assign C2 = decoder_1_out4 ? xor4_1_c2 : 1'bz;  // Controlled_Buffer controlled_buffer_15
  assign C3 = decoder_1_out4 ? xor4_1_c3 : 1'bz;  // Controlled_Buffer controlled_buffer_16
  or or_1 (or_1_out, decoder_1_out2, decoder_1_out1);
  assign C0 = or_1_out ? add_sub_1_s0 : 1'bz;  // Controlled_Buffer controlled_buffer_17
  assign C1 = or_1_out ? add_sub_1_s1 : 1'bz;  // Controlled_Buffer controlled_buffer_18
  assign C2 = or_1_out ? add_sub_1_s2 : 1'bz;  // Controlled_Buffer controlled_buffer_19
  assign C3 = or_1_out ? add_sub_1_s3 : 1'bz;  // Controlled_Buffer controlled_buffer_20
  assign Carry = or_1_out ? add_sub_1_carry : 1'bz;  // Controlled_Buffer controlled_buffer_21
  assign Greater_Than = decoder_1_out3 ? add_sub_1_gt : 1'bz;  // Controlled_Buffer controlled_buffer_22
  assign Equal = decoder_1_out3 ? add_sub_1_eq : 1'bz;  // Controlled_Buffer controlled_buffer_23
  assign Less_Than = decoder_1_out3 ? add_sub_1_lt : 1'bz;  // Controlled_Buffer controlled_buffer_24

  // Notes on the sheet:
  //   0000 - NONE
  //   0001 - ADD
  //   0100 - XOR
  //   0110 - ASL
  //   0111 - ASR
  //   INSTRUCTION COMMANDS:
  //   0010 - SUBTRACT
  //   0011 - COMPARE
  //   0101 - TWOS COMPLEMENT
endmodule

module test_ALU (
  input  A_ENABLE,
  input  CLK,
  input  A_WE,
  input  A0,
  input  A1,
  input  A2,
  input  in_7,
  input  A3,
  input  in_9,
  input  in_10,
  input  in_11,
  input  B_ENABLE,
  input  B_WE,
  input  B0,
  input  B1,
  input  B2,
  input  B3,
  input  C_WE,
  output out_19,
  output out_20,
  output out_21,
  output out_22,
  output out_23,
  output out_24,
  output out_25,
  output out_26,
  output out_27,
  output out_28,
  output out_29,
  output out_30
);

  wire A_q0, A_q1, A_q2, A_q3, B_q0, B_q1, B_q2, B_q3, controlled_buffer_1_out, controlled_buffer_2_out,
       controlled_buffer_3_out, controlled_buffer_4_out, controlled_buffer_5_out, controlled_buffer_6_out,
       controlled_buffer_7_out, controlled_buffer_8_out, main_1_c0, main_1_c1, main_1_c2, main_1_c3;

  REG4 A (
    .CLK(CLK), .ENABLE(A_WE), .D0(A0), .D1(A1), .D2(A2), .D3(A3), .Q0(A_q0), .Q1(A_q1), .Q2(A_q2), .Q3(A_q3));  // open: NOT_Q0, NOT_Q1, NOT_Q2, NOT_Q3
  REG4 B (
    .CLK(CLK), .ENABLE(B_WE), .D0(B0), .D1(B1), .D2(B2), .D3(B3), .Q0(B_q0), .Q1(B_q1), .Q2(B_q2), .Q3(B_q3));  // open: NOT_Q0, NOT_Q1, NOT_Q2, NOT_Q3
  assign controlled_buffer_1_out = A_ENABLE ? A_q3 : 1'bz;  // Controlled_Buffer controlled_buffer_1
  assign controlled_buffer_2_out = A_ENABLE ? A_q2 : 1'bz;  // Controlled_Buffer controlled_buffer_2
  assign controlled_buffer_3_out = A_ENABLE ? A_q1 : 1'bz;  // Controlled_Buffer controlled_buffer_3
  assign controlled_buffer_4_out = A_ENABLE ? A_q0 : 1'bz;  // Controlled_Buffer controlled_buffer_4
  assign controlled_buffer_5_out = B_ENABLE ? B_q3 : 1'bz;  // Controlled_Buffer controlled_buffer_5
  assign controlled_buffer_6_out = B_ENABLE ? B_q2 : 1'bz;  // Controlled_Buffer controlled_buffer_6
  assign controlled_buffer_7_out = B_ENABLE ? B_q1 : 1'bz;  // Controlled_Buffer controlled_buffer_7
  assign controlled_buffer_8_out = B_ENABLE ? B_q0 : 1'bz;  // Controlled_Buffer controlled_buffer_8
  main main_1 (
    .A3(controlled_buffer_1_out), .A2(controlled_buffer_2_out), .A1(controlled_buffer_3_out),
    .A0(controlled_buffer_4_out), .I3(in_7), .I2(in_9), .I1(in_10), .I0(in_11), .B3(controlled_buffer_5_out),
    .B2(controlled_buffer_6_out), .B1(controlled_buffer_7_out), .B0(controlled_buffer_8_out), .C0(main_1_c0),
    .C1(main_1_c1), .C2(main_1_c2), .C3(main_1_c3), .Carry(out_19), .Greater_Than(out_20), .Equal(out_21),
    .Less_Than(out_22));
  REG4 C (
    .CLK(CLK), .ENABLE(C_WE), .D0(main_1_c0), .D1(main_1_c1), .D2(main_1_c2), .D3(main_1_c3), .Q0(out_23),
    .NOT_Q0(out_24), .Q1(out_25), .NOT_Q1(out_26), .Q2(out_27), .NOT_Q2(out_28), .Q3(out_29), .NOT_Q3(out_30));
endmodule
